// Logisim project Exponent Difference.circ as structural Verilog: 7 circuits, main circuit Exponent_Comparator
module Exponent_Comparator (
  input  [3:0] Exponent_1,
  input  [3:0] Exponent_2,
  output [3:0] Exponent_out
);

  wire comparator_1_lt;

  Comparator #(.width(4)) comparator_1 (.a(Exponent_1), .b(Exponent_2), .lt(comparator_1_lt));  // open: gt, eq
  Multiplexer #(.width(4), .enable("false")) multiplexer_1 (
    .in0(Exponent_1), .in1(Exponent_2), .out(Exponent_out), .sel(comparator_1_lt));
endmodule

module Exponent_difference (
  input  [3:0] Exponent_1,
  input  [3:0] Exponent_2,
  output [3:0] Exponent_Difference
);

  wire subtractor_1_bout, xor_1_out;
  wire [3:0] adder_1_out, multiplexer_1_out, multiplexer_2_out, multiplexer_3_out, negator_1_out,
       negator_2_out, negator_3_out, subtractor_1_out;

  Negator #(.width(4)) negator_1 (.in(Exponent_1), .out(negator_1_out));
  Multiplexer #(.width(4), .enable("false")) multiplexer_1 (
    .in0(Exponent_1), .in1(negator_1_out), .out(multiplexer_1_out), .sel(Exponent_1[3]));
  Negator #(.width(4)) negator_2 (.in(Exponent_2), .out(negator_2_out));
  Subtractor #(.width(4)) subtractor_1 (
    .a(multiplexer_1_out), .b(multiplexer_2_out), .out(subtractor_1_out), .bin(1'b0), .bout(subtractor_1_bout));
  Adder_part #(.width(4)) adder_1 (
    .a(multiplexer_1_out), .b(multiplexer_2_out), .out(adder_1_out), .cin(1'b0));  // open: cout
  Multiplexer #(.width(4), .enable("false")) multiplexer_2 (
    .in0(Exponent_2), .in1(negator_2_out), .out(multiplexer_2_out), .sel(Exponent_2[3]));
  Negator #(.width(4)) negator_3 (.in(subtractor_1_out), .out(negator_3_out));
  Multiplexer #(.width(4), .enable("false")) multiplexer_3 (
    .in0(subtractor_1_out), .in1(negator_3_out), .out(multiplexer_3_out), .sel(subtractor_1_bout));
  xor xor_1 (xor_1_out, Exponent_1[3], Exponent_2[3]);
  Multiplexer #(.width(4), .enable("false")) multiplexer_4 (
    .in0(multiplexer_3_out), .in1(adder_1_out), .out(Exponent_Difference), .sel(xor_1_out));
endmodule

module Shifter (
  input  [15:0] Fraction1,
  input  [15:0] Fraction_2,
  input  [3:0] Bits_to_Shift,
  input  A_B,
  output [15:0] Fraction_1_out,
  output [15:0] Fraction_2_out
);

  wire [15:0] shifter_1_out, shifter_2_out;

  Shifter_part #(.width(16), .shift("lr")) shifter_1 (.in(Fraction1), .\dist (Bits_to_Shift), .out(shifter_1_out));
  Multiplexer #(.width(16), .enable("false")) multiplexer_1 (
    .in0(shifter_1_out), .in1(Fraction1), .out(Fraction_1_out), .sel(A_B));
  Shifter_part #(.width(16), .shift("lr")) shifter_2 (.in(Fraction_2), .\dist (Bits_to_Shift), .out(shifter_2_out));
  Multiplexer #(.width(16), .enable("false")) multiplexer_2 (
    .in0(Fraction_2), .in1(shifter_2_out), .out(Fraction_2_out), .sel(A_B));
endmodule

module Adder (
  input  [15:0] Fraction_1,
  input  [15:0] Fraction_2,
  input  Sign_1,
  input  Sign_2,
  output Sign_out,
  output [15:0] Fraction_sum,
  output Carry_out
);

  wire and_1_out, and_2_out, and_3_out, comparator_1_gt, comparator_1_lt, subtractor_1_bout, xor_1_out;
  wire [15:0] adder_1_out, multiplexer_1_out, negator_1_out, subtractor_1_out;

  xor xor_1 (xor_1_out, Sign_1, Sign_2);
  Comparator #(.width(16), .mode("unsigned")) comparator_1 (
    .a(Fraction_1), .b(Fraction_2), .gt(comparator_1_gt), .lt(comparator_1_lt));  // open: eq
  Adder_part #(.width(16)) adder_1 (.a(Fraction_1), .b(Fraction_2), .out(adder_1_out), .cin(1'b0), .cout(Carry_out));
  Subtractor #(.width(16)) subtractor_1 (
    .a(Fraction_1), .b(Fraction_2), .out(subtractor_1_out), .bin(1'b0), .bout(subtractor_1_bout));
  Negator #(.width(16)) negator_1 (.in(subtractor_1_out), .out(negator_1_out));
  and and_1 (and_1_out, comparator_1_gt, Sign_1);
  and and_2 (and_2_out, comparator_1_lt, Sign_2);
  and and_3 (and_3_out, Sign_1, Sign_2);
  Multiplexer #(.width(16), .enable("false")) multiplexer_1 (
    .in0(subtractor_1_out), .in1(negator_1_out), .out(multiplexer_1_out), .sel(subtractor_1_bout));
  or or_1 (Sign_out, and_1_out, and_2_out, and_3_out);
  Multiplexer #(.width(16), .enable("false")) multiplexer_2 (
    .in0(adder_1_out), .in1(multiplexer_1_out), .out(Fraction_sum), .sel(xor_1_out));
endmodule

module Normalize (
  input  [3:0] Exponent_in,
  input  [15:0] Fraction_in,
  input  Carry_in,
  output [15:0] Fraction_out,
  output [3:0] Exponent_out
);

  wire adder_1_cout, comparator_1_gt, or_1_out, subtractor_1_bout;
  wire [3:0] adder_1_out, bitfinder_1_index, multiplexer_1_out, negator_1_out, subtractor_1_out,
       subtractor_2_out;
  wire [15:0] multiplexer_3_out, shifter_1_out;

  Comparator #(.width(4), .mode("unsigned")) comparator_1 (
    .a(multiplexer_1_out), .b(4'b0111), .gt(comparator_1_gt));  // open: eq, lt
  Subtractor #(.width(4)) subtractor_1 (
    .a(Exponent_in), .b(adder_1_out), .out(subtractor_1_out), .bin(1'b0), .bout(subtractor_1_bout));
  Negator #(.width(4)) negator_1 (.in(subtractor_1_out), .out(negator_1_out));
  Multiplexer #(.width(4), .enable("false")) multiplexer_1 (
    .in0(subtractor_1_out), .in1(negator_1_out), .out(multiplexer_1_out), .sel(subtractor_1_bout));
  Multiplexer #(.width(4), .enable("false")) multiplexer_2 (
    .in0(multiplexer_1_out), .in1(4'b0000), .out(Exponent_out), .sel(comparator_1_gt));
  BitFinder #(.width(16), .\type ("high1")) bitfinder_1 (.in(Fraction_in), .index(bitfinder_1_index));  // open: found
  Shifter_part #(.width(16)) shifter_1 (.in(Fraction_in), .\dist (adder_1_out), .out(shifter_1_out));
  Multiplexer #(.width(16), .enable("false")) multiplexer_3 (
    .in0(shifter_1_out), .in1(Fraction_in), .out(multiplexer_3_out), .sel(Carry_in));
  or or_1 (or_1_out, comparator_1_gt, adder_1_cout);
  Multiplexer #(.width(16), .enable("false")) multiplexer_4 (
    .in0(multiplexer_3_out), .in1({16{1'b0}}), .out(Fraction_out), .sel(or_1_out));
  Subtractor #(.width(4)) subtractor_2 (
    .a(4'b1111), .b(bitfinder_1_index), .out(subtractor_2_out), .bin(1'b0));  // open: bout
  Adder_part #(.width(4)) adder_1 (
    .a(subtractor_2_out), .b(4'b0001), .out(adder_1_out), .cin(1'b0), .cout(adder_1_cout));
endmodule

module Preformatter (
  input  [15:0] Input_in,
  output Sign_bit,
  output [3:0] Exponent,
  output [15:0] Fraction
);


  assign Exponent = Input_in[14:11];
  assign Fraction = {1'b1, Input_in[10:0], 4'b0000};
  assign Sign_bit = Input_in[15];
endmodule

module main (
  input  [15:0] in_1,
  input  [15:0] in_2,
  input  in_3,
  output out_4,
  output [3:0] out_5,
  output [15:0] out_6
);

  wire adder_1_carry_out, preformatter_1_sign_bit, preformatter_2_sign_bit;
  wire [3:0] exponent_comparator_1_exponent_out, exponent_difference_1_exponent_difference,
       preformatter_1_exponent, preformatter_2_exponent;
  wire [15:0] adder_1_fraction_sum, preformatter_1_fraction, preformatter_2_fraction,
       shifter_1_fraction_1_out, shifter_1_fraction_2_out;

  Preformatter preformatter_1 (
    .Input_in(in_1), .Sign_bit(preformatter_1_sign_bit), .Exponent(preformatter_1_exponent),
    .Fraction(preformatter_1_fraction));
  Exponent_difference exponent_difference_1 (
    .Exponent_1(preformatter_1_exponent), .Exponent_2(preformatter_2_exponent),
    .Exponent_Difference(exponent_difference_1_exponent_difference));
  Exponent_Comparator exponent_comparator_1 (
    .Exponent_1(preformatter_1_exponent), .Exponent_2(preformatter_2_exponent),
    .Exponent_out(exponent_comparator_1_exponent_out));
  Shifter shifter_1 (
    .Bits_to_Shift(exponent_difference_1_exponent_difference), .A_B(in_3),
    .Fraction1(preformatter_1_fraction), .Fraction_2(preformatter_2_fraction),
    .Fraction_1_out(shifter_1_fraction_1_out), .Fraction_2_out(shifter_1_fraction_2_out));
  Adder adder_1 (
    .Sign_1(preformatter_1_sign_bit), .Sign_2(preformatter_2_sign_bit),
    .Fraction_1(shifter_1_fraction_1_out), .Fraction_2(shifter_1_fraction_2_out), .Sign_out(out_4),
    .Fraction_sum(adder_1_fraction_sum), .Carry_out(adder_1_carry_out));
  Preformatter preformatter_2 (
    .Input_in(in_2), .Sign_bit(preformatter_2_sign_bit), .Exponent(preformatter_2_exponent),
    .Fraction(preformatter_2_fraction));
  Normalize normalize_1 (
    .Carry_in(adder_1_carry_out), .Exponent_in(exponent_comparator_1_exponent_out),
    .Fraction_in(adder_1_fraction_sum), .Exponent_out(out_5), .Fraction_out(out_6));
endmodule
