// Logisim project fp_adder_offline.circ as structural Verilog: 8 circuits, main circuit main
module main (
  input  [15:0] Input_A,
  input  [15:0] Input_B,
  output [15:0] Output,
  output Overflow_Flag,
  output Underflow_Flag
);

  fp_adder fp_adder_1 (
    .in_1(Input_A), .in_2(Input_B), .Underflow_Flag(Underflow_Flag), .Final_Answer(Output),
    .Overflow_Flag(Overflow_Flag));
endmodule

// Floating Point Adder
module fp_adder (
  input  [15:0] in_1,
  input  [15:0] in_2,
  output Underflow_Flag,
  output Overflow_Flag,
  output [15:0] Final_Answer
);

  wire comparator_1__1st_input___2nd_input, xor_1_out;
  wire [3:0] comparator_1_exponent_difference, multiplexer_1_out;
  wire [14:0] multiplexer_2_out, multiplexer_3_out, partioner_1_fraction, partioner_2_fraction, shifter_1_out;
  wire [15:0] adder_1_out, bit_inverter_1_out_3, normalizer_1_fraction_out;

  Multiplexer #(.width(4), .enable("false")) multiplexer_1 (
    .in0(in_1[14:11]), .in1(in_2[14:11]), .out(multiplexer_1_out), .sel(comparator_1__1st_input___2nd_input));
  partioner partioner_1 (.Fraction(partioner_1_fraction), .Input(in_1[10:0]));
  comparator comparator_1 (
    .in_1(in_1[10:0]), .in_2(in_1[14:11]), .in_3(in_2[10:0]), .in_4(in_2[14:11]),
    .Exponent_Difference(comparator_1_exponent_difference),
    ._1st_input___2nd_input(comparator_1__1st_input___2nd_input));
  partioner partioner_2 (.Fraction(partioner_2_fraction), .Input(in_2[10:0]));
  Multiplexer #(.width(15), .enable("false")) multiplexer_2 (
    .in0(partioner_1_fraction), .in1(partioner_2_fraction), .out(multiplexer_2_out),
    .sel(comparator_1__1st_input___2nd_input));
  normalizer normalizer_1 (
    .Fraction_In(adder_1_out), .Exponent_In(multiplexer_1_out), .Fraction_Out(normalizer_1_fraction_out),
    .Exponent_Out(Final_Answer[14:11]), .Overflow_Flag(Overflow_Flag), .Underflow_Flag(Underflow_Flag));
  Multiplexer #(.width(15), .enable("false")) multiplexer_3 (
    .in0(partioner_2_fraction), .in1(partioner_1_fraction), .out(multiplexer_3_out),
    .sel(comparator_1__1st_input___2nd_input));
  xor xor_1 (xor_1_out, in_2[15], in_1[15]);
  Shifter #(.width(15), .shift("lr")) shifter_1 (
    .in(multiplexer_3_out), .\dist (comparator_1_exponent_difference), .out(shifter_1_out));
  Adder #(.width(16)) adder_1 (
    .a({1'b0, multiplexer_2_out}), .b(bit_inverter_1_out_3), .out(adder_1_out), .cin(1'b0));  // open: cout
  truncation_hardware truncation_hardware_1 (
    .Fraction_Out(Final_Answer[10:0]), .Fraction_In(normalizer_1_fraction_out));
  Multiplexer #(.enable("false")) multiplexer_4 (
    .in0(in_1[15]), .in1(in_2[15]), .out(Final_Answer[15]), .sel(comparator_1__1st_input___2nd_input));
  bit_inverter bit_inverter_1 (.in_1(shifter_1_out), .in_2(xor_1_out), .out_3(bit_inverter_1_out_3));
endmodule

// Partitioner
module partioner (
  input  [10:0] Input,
  output [14:0] Fraction
);


  assign Fraction = {1'b1, Input, 3'b000};
endmodule

module comparator (
  input  [10:0] in_1,
  input  [3:0] in_2,
  input  [10:0] in_3,
  input  [3:0] in_4,
  output [3:0] Exponent_Difference,
  output _1st_input___2nd_input
);

  wire subtractor_3_bout;
  wire [3:0] negator_1_out, subtractor_1_out, subtractor_2_out, subtractor_3_out;

  Subtractor #(.width(4)) subtractor_1 (.a(in_2), .b(4'b0111), .out(subtractor_1_out), .bin(1'b0));  // open: bout
  Subtractor #(.width(4)) subtractor_2 (.a(in_4), .b(4'b0111), .out(subtractor_2_out), .bin(1'b0));  // open: bout
  Comparator #(.width(15), .mode("unsigned")) comparator_1 (
    .a({subtractor_1_out, in_1}), .b({subtractor_2_out, in_3}), .lt(_1st_input___2nd_input));  // open: gt, eq
  Subtractor #(.width(4)) subtractor_3 (
    .a(subtractor_1_out), .b(subtractor_2_out), .out(subtractor_3_out), .bin(1'b0), .bout(subtractor_3_bout));
  Negator #(.width(4)) negator_1 (.in(subtractor_3_out), .out(negator_1_out));
  Multiplexer #(.width(4), .enable("false")) multiplexer_1 (
    .in0(subtractor_3_out), .in1(negator_1_out), .out(Exponent_Difference), .sel(subtractor_3_bout));
endmodule

// Bit Inverter
module bit_inverter (
  input  [14:0] in_1,
  input  in_2,
  output [15:0] out_3
);

  wire [15:0] negator_1_out;

  Negator #(.width(16)) negator_1 (.in({1'b0, in_1}), .out(negator_1_out));
  Multiplexer #(.width(16), .enable("false")) multiplexer_1 (
    .in0({1'b0, in_1}), .in1(negator_1_out), .out(out_3), .sel(in_2));
endmodule

// Leading 1 Finder
module leading_one_finder (
  input  [15:0] in_1,
  output [3:0] out_2,
  output out_3
);

  wire [3:0] bitfinder_1_index;

  BitFinder #(.width(16), .\type ("high1")) bitfinder_1 (.in(in_1), .index(bitfinder_1_index), .found(out_3));
  Subtractor #(.width(4)) subtractor_1 (.a(4'b1110), .b(bitfinder_1_index), .out(out_2), .bin(1'b0));  // open: bout
endmodule

// Normalizer
module normalizer (
  input  [15:0] Fraction_In,
  input  [3:0] Exponent_In,
  output [15:0] Fraction_Out,
  output [3:0] Exponent_Out,
  output Overflow_Flag,
  output Underflow_Flag
);

  wire and_1_out, and_2_out, comparator_1_gt, comparator_2_eq, comparator_2_lt, leading_one_finder_1_out_3,
       not_1_out, or_1_out;
  wire [3:0] leading_one_finder_1_out_2;
  wire [4:0] adder_1_out, multiplexer_3_out, subtractor_1_out;
  wire [4:4] multiplexer_4_out;
  wire [15:0] multiplexer_1_out, shifter_1_out, shifter_2_out;

  Subtractor #(.width(5)) subtractor_1 (
    .a({1'b0, Exponent_In}), .b({1'b0, leading_one_finder_1_out_2}), .out(subtractor_1_out), .bin(1'b0));  // open: bout
  leading_one_finder leading_one_finder_1 (
    .in_1(Fraction_In), .out_2(leading_one_finder_1_out_2), .out_3(leading_one_finder_1_out_3));
  Adder #(.width(5)) adder_1 (.a({1'b0, Exponent_In}), .b(5'b00001), .out(adder_1_out), .cin(1'b0));  // open: cout
  Shifter #(.width(16)) shifter_1 (.in(Fraction_In), .\dist (leading_one_finder_1_out_2), .out(shifter_1_out));
  Shifter #(.width(16), .shift("lr")) shifter_2 (.in(Fraction_In), .\dist (4'b0001), .out(shifter_2_out));
  and and_1 (and_1_out, leading_one_finder_1_out_2[0], leading_one_finder_1_out_2[1], leading_one_finder_1_out_2[2], leading_one_finder_1_out_2[3]);
  not not_1 (not_1_out, and_1_out);
  Multiplexer #(.width(16), .enable("false")) multiplexer_1 (
    .in0(shifter_1_out), .in1(shifter_2_out), .out(multiplexer_1_out), .sel(and_1_out));
  Multiplexer #(.width(16), .enable("false")) multiplexer_2 (
    .in0(Fraction_In), .in1(multiplexer_1_out), .out(Fraction_Out), .sel(leading_one_finder_1_out_3));
  Comparator #(.width(5)) comparator_1 (
    .a({multiplexer_4_out[4], Exponent_Out}), .b(5'b01110), .gt(comparator_1_gt));  // open: eq, lt
  Comparator #(.width(5)) comparator_2 (
    .a({multiplexer_4_out[4], Exponent_Out}), .b({5{1'b0}}), .eq(comparator_2_eq), .lt(comparator_2_lt));  // open: gt
  Multiplexer #(.width(5), .enable("false")) multiplexer_3 (
    .in0(subtractor_1_out), .in1(adder_1_out), .out(multiplexer_3_out), .sel(and_1_out));
  Multiplexer #(.width(5), .enable("false")) multiplexer_4 (
    .in0({1'b0, Exponent_In}), .in1(multiplexer_3_out), .out({multiplexer_4_out[4], Exponent_Out}),
    .sel(leading_one_finder_1_out_3));
  or or_1 (or_1_out, comparator_2_eq, comparator_2_lt);
  and and_2 (and_2_out, Exponent_Out[0], Exponent_Out[1], Exponent_Out[2], Exponent_Out[3], not_1_out);
  and and_3 (Overflow_Flag, comparator_1_gt, and_1_out);
  or or_2 (Underflow_Flag, or_1_out, and_2_out);
endmodule

// Truncation Hardware
module truncation_hardware (
  input  [15:0] Fraction_In,
  output [10:0] Fraction_Out
);


  assign Fraction_Out = Fraction_In[13:3];
endmodule
