// Logisim project sizvy_part.circ as structural Verilog: 2 circuits, main circuit Right Shifter
module Right_Shifter (
  input  [14:0] Input,
  input  [3:0] Shift_Amount,
  output [14:0] out_3
);

  Shifter_part #(.width(15), .shift("lr")) shifter_1 (.in(Input), .\dist (Shift_Amount), .out(out_3));
endmodule

module Shifter (
  input  [15:0] Input,
  input  [3:0] Shift_amount,
  output [15:0] Output
);

  wire [15:0] shifter_1_out;

  Shifter_part #(.width(16), .shift("rl")) shifter_1 (
    .in(Input), .\dist (Shift_amount), .out({shifter_1_out[15], Output[14:1], shifter_1_out[0]}));
  or or_1 (Output[0], shifter_1_out[0], shifter_1_out[15]);

  assign Output[15] = 1'b0;
endmodule
